# Fritzing sketch sketch (saved by Fritzing 0.9.3b)
perfboards: 1

parts:
  R1 = Resistor [tolerance=±5% resistance=10k package="0603 [SMD]"]
  Display_OLED_I2C = OLED Monochrome 128x32 I2C [part_number=931]
  Navigation_Switch = Pushbutton [package="[THT]"]
  Action_switch = Pushbutton [package="[THT]"]
  Arduino_Nano = Arduino Nano (Rev3.0)
  Source_5V = DC Power [voltage=5]
  DHT11 = DHT11 Humitidy and Temperature Sensor

nets:
  VIN: R1.Pin_0, Display_OLED_I2C.VIN, Arduino_Nano.5V, Source_5V.V+, DHT11.VDD
  N1: R1.Pin_1, Arduino_Nano.D9, DHT11.DATA
  GND: Display_OLED_I2C.GND, Navigation_Switch.Pin_1, Navigation_Switch.Pin_2, Action_switch.Pin_1, Action_switch.Pin_2, Arduino_Nano.GND
  N2: Display_OLED_I2C.SCL, Arduino_Nano.A5
  N3: Display_OLED_I2C.SDA, Arduino_Nano.A4
  N4: Navigation_Switch.Pin_3, Navigation_Switch.Pin_4, Arduino_Nano.D2
  N5: Action_switch.Pin_3, Action_switch.Pin_4, Arduino_Nano.D3

custom parts:
  OLED Monochrome 128x32 I2C: These displays are small, only about 1" diagonal, but very readable due to the high contrast of an OLED display. This display is made of 128x32 individual white OLED pixels, each one is turned on or off by the controller chip. Because the display makes its own light, no backlight is required. This reduces the power required to run the OLED and is why the display has such high contrast; we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
  DHT11 Humitidy and Temperature Sensor: DHT11 Humidity and Temperature Sensor
